# Fritzing sketch SmartScale (saved by Fritzing 0.9.3b)
breadboards: 2

parts:
  BUTTON_BLUE = Arcade Button (blue)
  Part2 = HX711 Weighing Sensor Module
  J1 = LOAD_CELL [package=1x03]
  J2 = LOAD_CELL [package=1x03]
  J3 = LOAD_CELL [package=1x03]
  J4 = LOAD_CELL [package=1x03]
  Part5 = Adafruit Feather HUZZAH ESP8266 [part_number="Adafruit #2821"]
  Q2 = PNP-Transistor [package="TO92 [THT]"]
  Q3 = PNP-Transistor [package="TO92 [THT]"]
  Q4 = NPN-Transistor [package="TO92 [THT]"]
  R2 = Resistor [tolerance=±5% resistance=10k package=THT]
  R3 = Resistor [tolerance=±5% resistance=10k package=THT]
  R4 = Resistor [tolerance=±5% resistance=10k package=THT]
  R5 = Resistor [tolerance=±5% resistance=10k package=THT]
  BUTTON_YELLOW = Arcade Button (blue)
  MAX7219_LED_Matrix = 8x8 LED Modul mit MAX7219 [package=THT]

nets:
  N1: BUTTON_BLUE.BTN+, Part5.GPIO4/SDA, R3.Pin_0
  GND: BUTTON_BLUE.BTN-, BUTTON_BLUE.LED-, Part2.GND, Part5.GND, Q4.E, BUTTON_YELLOW.BTN-, BUTTON_YELLOW.LED-, MAX7219_LED_Matrix.GND_Eingang
  N2: BUTTON_BLUE.LED+, Part5.GPIO15
  VCC: Part2.VCC, Part5.3.3V, R5.Pin_0, MAX7219_LED_Matrix.VCC_Eingang
  N3: Part2.DO/RX, Part5.TXD
  N4: Part2.CK/TX, Part5.GPIO2
  N5: Part2.E+, J4.W
  N6: Part2.E-, J1.W
  N7: Part2.A+, J3.W
  N8: Part2.A-, J2.W
  N9: J1.B, J2.B
  N10: J1.R, J4.R
  N11: J2.R, J3.R
  N12: J3.B, J4.B
  N13: Part5.GPIO12/MISO, MAX7219_LED_Matrix.CS_Eingang
  N14: Part5.GPIO13/MOSI, MAX7219_LED_Matrix.DIN_Eingang
  N15: Part5.GPIO14/SCK, MAX7219_LED_Matrix.CLK_Eingang
  N16: Part5.RESET, Q2.E, Q3.E
  N17: Part5.GPIO0, R4.Pin_0, R5.Pin_1
  N18: Part5.GPIO16, BUTTON_YELLOW.LED+
  N19: Part5.GPIO5/SCL, R2.Pin_0, BUTTON_YELLOW.BTN+
  N20: Q2.B, R2.Pin_1
  N21: Q2.C, Q3.C, Q4.C
  N22: Q3.B, R3.Pin_1
  N23: Q4.B, R4.Pin_1

custom parts:
  Arcade Button (blue): Adafruit Arcade Button (blue)
  Adafruit Feather HUZZAH ESP8266: his is the Adafruit Feather HUZZAH ESP8266 - our take on an 'all-in-one' ESP8266 WiFi development board with built in USB and battery charging. Its an ESP8266 WiFi module with all the extras you need, ready to rock! We have other boards in the Feather family, check'em out here. At the Feather HUZZAH's heart is an ESP8266 WiFi microcontroller clocked at 80 MHz and at 3.3V logic. This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
