# Fritzing sketch ESP-01 Flasher (saved by Fritzing 0.9.3b)
breadboards: 1

parts:
  Part1 = FTDI Basic Programmer
  U1 = ESP8266 WiFi Module [part_number=ESP8266]
  S1 = Pushbutton [package="[THT]"]
  S2 = Pushbutton [package="[THT]"]
  R1 = Resistor [tolerance=±5% resistance=1k package=THT]
  R2 = Resistor [tolerance=±5% resistance=1k package=THT]

nets:
  N1: Part1.RXI, U1.TXD
  N2: Part1.TXO, U1.RXD
  N3: Part1.POWER, U1.VCC, R2.Pin_1
  GND: Part1.GND, U1.GND, S2.Pin_1, S2.Pin_2, R1.Pin_1
  N4: U1.GPIO_0, S2.Pin_3, S2.Pin_4
  N5: U1.RST, S1.Pin_1, S1.Pin_2
  N6: U1.CH_PD, R2.Pin_0
  N7: S1.Pin_3, S1.Pin_4, R1.Pin_0

notes:
  RST
  GP0

custom parts:
  ESP8266 WiFi Module: Generic WiFi Module based on the ESP8266 with onboard PCB antenna and UART communications
  Pushbutton: A generic pushbutton.
