# Fritzing sketch SmartScale (saved by Fritzing 0.9.3b)
breadboards: 2

parts:
  BUTTON_BLUE = Arcade Button (blue)
  Part2 = HX711 Weighing Sensor Module
  J1 = LOAD_CELL [package=1x03]
  J2 = LOAD_CELL [package=1x03]
  J3 = LOAD_CELL [package=1x03]
  J4 = LOAD_CELL [package=1x03]
  Part5 = Adafruit Feather HUZZAH ESP8266 [part_number="Adafruit #2821"]
  Q2 = PNP-Transistor [package="TO92 [THT]"]
  Q3 = PNP-Transistor [package="TO92 [THT]"]
  Q4 = NPN-Transistor [package="TO92 [THT]"]
  R2 = Resistor [tolerance=±5% resistance=10k package=THT]
  R3 = Resistor [tolerance=±5% resistance=10k package=THT]
  R5 = Resistor [tolerance=±5% resistance=10k package=THT]
  BUTTON_YELLOW = Arcade Button (blue)
  MAX7219_LED_Matrix = 8x8 LED Modul mit MAX7219 [package=THT]
  Q5 = PNP-Transistor [package="TO92 [THT]"]
  Q6 = PNP-Transistor [package="TO92 [THT]"]
  U2 = Voltage Regulator [package=v-reg_dpack]
  Q7 = NPN-Transistor [package="TO92 [THT]"]
  Q8 = NPN-Transistor [package="TO92 [THT]"]
  R4 = Resistor [tolerance=±5% resistance=100k package=THT]
  R7 = Resistor [tolerance=±5% resistance=220 package=THT]
  R6 = Resistor [tolerance=±5% resistance=220 package=THT]
  R8 = Resistor [tolerance=±5% resistance=1k package=THT]
  R10 = Resistor [tolerance=±5% resistance=1M package=THT]
  R9 = Resistor [tolerance=±5% resistance=220k package=THT]
  Q9 = NPN-Transistor [package="TO92 [THT]"]
  R11 = Resistor [tolerance=±5% resistance=100k package=THT]
  R12 = Resistor [tolerance=±5% resistance=100k package=THT]
  Q10 = NPN-Transistor [package="TO92 [THT]"]
  J5 = female pin header, 3 pins [form="♀ (female)"]
  J6 = female pin header, 5 pins [form="♀ (female)"]

nets:
  N1: BUTTON_BLUE.BTN+, Part5.GPIO4/SDA, R3.Pin_0
  GND: BUTTON_BLUE.BTN-, BUTTON_BLUE.LED-, Part2.GND, Part5.GND, Q4.E, BUTTON_YELLOW.BTN-, BUTTON_YELLOW.LED-, MAX7219_LED_Matrix.GND_Eingang, U2.GND, R7.Pin_1, R6.Pin_1, R9.Pin_1, J5.pin1
  N2: BUTTON_BLUE.LED+, Q5.C
  VCC: Part2.VCC, Part5.3.3V, R5.Pin_0, U2.VIN, R8.Pin_0, J6.pin1
  N3: Part2.DO/RX, Part5.GPIO2
  N4: Part2.CK/TX, Part5.GPIO12/MISO
  N5: Part2.E+, J4.W
  N6: Part2.E-, J1.W
  N7: Part2.A+, J3.W
  N8: Part2.A-, J2.W
  N9: J1.B, J2.B
  N10: J1.R, J4.R
  N11: J2.R, J3.R
  N12: J3.B, J4.B
  N13: Part5.TXD, MAX7219_LED_Matrix.CS_Eingang
  N14: Part5.GPIO13/MOSI, MAX7219_LED_Matrix.DIN_Eingang
  N15: Part5.GPIO14/SCK, MAX7219_LED_Matrix.CLK_Eingang
  N16: Part5.ADC, R10.Pin_0, R9.Pin_0, J5.pin2
  N17: Part5.RESET, Q2.E, Q3.E, R8.Pin_1
  N18: Part5.VBAT, R10.Pin_1, J5.pin3
  N19: Part5.GPIO15, Q7.B, Q10.C
  N20: Part5.GPIO0, R5.Pin_1, R4.Pin_0, R11.Pin_0, R12.Pin_0, J6.pin2, J6.pin3
  N21: Part5.GPIO16, Q8.B, Q9.C
  N22: Part5.GPIO5/SCL, R2.Pin_0, BUTTON_YELLOW.BTN+
  N23: Q2.B, R2.Pin_1
  N24: Q2.C, Q3.C, Q4.C
  N25: Q3.B, R3.Pin_1
  N26: Q4.B, R4.Pin_1
  N27: BUTTON_YELLOW.LED+, Q6.C
  N28: MAX7219_LED_Matrix.VCC_Eingang, Q5.E, Q6.E, U2.VOUT
  N29: Q5.B, Q7.C
  N30: Q6.B, Q8.C
  N31: Q7.E, R6.Pin_0, Q10.E
  N32: Q8.E, R7.Pin_0, Q9.E
  N33: Q9.B, R11.Pin_1, J6.pin4
  N34: R12.Pin_1, Q10.B, J6.pin5

custom parts:
  Arcade Button (blue): Adafruit Arcade Button (blue)
  Adafruit Feather HUZZAH ESP8266: his is the Adafruit Feather HUZZAH ESP8266 - our take on an 'all-in-one' ESP8266 WiFi development board with built in USB and battery charging. Its an ESP8266 WiFi module with all the extras you need, ready to rock! We have other boards in the Feather family, check'em out here. At the Feather HUZZAH's heart is an ESP8266 WiFi microcontroller clocked at 80 MHz and at 3.3V logic. This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
  Voltage Regulator: Voltage Regulator Standard LM317 adjustable voltage regulator. AOI (Adjust Output Input). Google 'LM317 Calculator' for easy to use app to get the two resistor values needed. 240/720 for 5V output. 240/390 for 3.3V output. Spark Fun Electronics SKU : COM-00527
