# Fritzing sketch Wake Light (saved by Fritzing 0.9.3b)

parts:
  LED1 = LED - 5mm [color="Red (633nm)" package="5 mm [THT]"]
  R1 = Resistor [tolerance=±1% resistance=22 package=THT]
  R2 = Resistor [tolerance=±1% resistance=47 package=THT]
  LED2 = LED - 5mm [color="Yellow (595nm)" package="5 mm [THT]"]
  J1 = female pin header, 5 pins [form="♀ (female)"]
  U1 = ESP8266 WiFi Module [part_number=ESP8266]
  J2 = Piezo Speaker
  R3 = Resistor [tolerance=±5% resistance=10k package=THT]
  U3 = Voltage Regulator - 5V [package="TO220 [THT]"]
  J3 = Power Jack [package=power_jack_slot]
  U4 = BUTTON-CONDUCTIVE [package=button-conductive-0.1]

nets:
  N1: LED1.cathode, LED2.cathode, J1.pin2, J1.pin4, U1.GPIO_2
  N2: LED1.anode, R1.Pin_0, R2.Pin_1, J1.pin5
  N3: R1.Pin_1, U1.VCC, J2.pin2, U3.output_voltage
  N4: R2.Pin_0, LED2.anode, J1.pin3, U4.2
  N5: J1.pin1, U1.GPIO_0, R3.Pin_0, U4.1
  GND: U1.GND, R3.Pin_1, U3.GND, J3.GND
  N6: U1.TXD, J2.pin1
  N7: U3.input_voltage, J3.PWR

custom parts:
  ESP8266 WiFi Module: Generic WiFi Module based on the ESP8266 with onboard PCB antenna and UART communications
  BUTTON-CONDUCTIVE: Used with rubber key pads. This one was designed and proven to work with the PolyCase Key FOB enclosures.
